// Logisim project Cantrell_Joseph.circ as structural Verilog: 8 circuits, main circuit main
module main (
);

  wire and_1_out, and_2_out, and_3_out, and_4_out, and_5_out, BNE, C, comparator_1_eq, comparator_2_eq,
       comparator_3_eq, comparator_4_eq, comparator_5_eq, comparator_6_eq, HALT, JLR, multiplexer_7_out,
       not_3_out, or_1_out, or_2_out, S, SRC;
  wire [1:1] PCSel;
  wire [3:0] DR3, DR4, DR5, OP3, SR1_3, SR2_2, SR2_3;
  wire [9:0] Control3, Control4, Control5, multiplexer_5_out;
  wire [9:1] rom_1_data;
  wire [19:0] OFF3;
  wire [31:0] A2, A3, adder_1_out, ALU3, ALU4, ALU5, B2, B3, B4, bit_extender_1_out, bit_extender_2_out,
       CalcPC2, CalcPC4, CalcPC5, FA2, FB2, IR2, MEM4, MEM5, MEM5_FW, multiplexer_1_out, multiplexer_2_out,
       PC2, PC3, PC_q, ram_2_data, RIn;

  Clock clock_1 (.out(C));
  // Probe on ALU4[23:0]
  // Probe on B4
  // Probe on PC2
  assign bit_extender_1_out = {{12{IR2[19]}}, IR2[19:0]};  // Bit_Extender bit_extender_1
  // Probe on IR2[19:0]
  // Probe on IR2[31:28]
  // Probe on OP3
  // Probe on B3
  Adder #(.width(32)) adder_1 (.a(32'h1), .b(PC_q), .out(adder_1_out));  // open: cin, cout
  // Probe on {PCSel[1], JLR}
  Adder #(.width(32)) adder_2 (.a(PC2), .b(bit_extender_1_out), .out(CalcPC2));  // open: cin, cout
  // Probe on IR2[3:0]
  // Probe on IR2[23:20]
  // Probe on IR2[27:24]
  not not_1 (HALT, rom_1_data[9]);
  ROM #(.addrWidth(4), .dataWidth(10)) rom_1 (
    .addr(IR2[31:28]), .data({rom_1_data[9:7], JLR, BNE, rom_1_data[4:1], SRC}));  // open: sel
  assign bit_extender_2_out = {{12{OFF3[19]}}, OFF3};  // Bit_Extender bit_extender_2
  // Probe on A3
  Multiplexer #(.select(2), .width(32), .enable("false")) multiplexer_1 (
    .in0(adder_1_out), .in1(FA2), .in2(CalcPC2), .in3(CalcPC2), .out(multiplexer_1_out), .sel({PCSel[1], JLR}));
  // Probe on multiplexer_2_out
  Multiplexer #(.width(32)) multiplexer_2 (
    .in0(B3), .in1(bit_extender_2_out), .out(multiplexer_2_out), .sel(Control3[2]));  // open: en
  ALU ALU (.A(A3), .B(multiplexer_2_out), .func(Control3[4:3]), .out_4(ALU3));
  RAM #(.addrWidth(24), .dataWidth(32), .bus("separate")) ram_1 (
    .addr(ALU4[23:0]), .din(B4), .data(MEM4), .str(Control4[7]), .clk(C), .ld(1'b1));  // open: sel, clr
  // Probe on RIn
  Multiplexer #(.width(32)) multiplexer_3 (.in0(ALU5), .in1(MEM5), .out(RIn), .sel(Control5[8]));  // open: en
  Register #(.width(32)) PC (.D(multiplexer_1_out), .en(S), .Q(PC_q), .clk(and_1_out));  // open: clr
  and and_1 (and_1_out, C, HALT);
  // Probe on RIn
  Multiplexer #(.width(4)) multiplexer_4 (.in0(IR2[3:0]), .in1(IR2[27:24]), .out(SR2_2), .sel(SRC));  // open: en
  // Probe on SR2_2
  Comparator #(.width(4)) comparator_1 (.a(4'b0101), .b(OP3), .eq(comparator_1_eq));  // open: gt, lt
  // Probe on OP3
  // Probe on SR2_2
  // Probe on IR2[23:20]
  or or_1 (or_1_out, comparator_3_eq, comparator_2_eq);
  not not_2 (S, and_2_out);
  and and_2 (and_2_out, comparator_1_eq, or_1_out);
  Multiplexer #(.width(10)) multiplexer_5 (
    .in0({rom_1_data[9:7], JLR, BNE, rom_1_data[4:1], SRC}), .in1(10'h23), .out(multiplexer_5_out),
    .sel(and_2_out));  // open: en
  // Probe on DR3
  // Probe on MEM4
  RAM #(.addrWidth(24), .dataWidth(32)) ram_2 (
    .addr(PC_q[23:0]), .data(ram_2_data), .clk(C), .ld(1'b1));  // open: sel, clr
  Dual_Ported_Register_File dual_ported_register_file_1 (
    .CLK(C), .WrEN(Control5[1]), .OUT1(A2), .WrREGNO(DR5), .RdREGNO1(IR2[23:20]), .RdREGNO2(SR2_2),
    .OUT2(B2), .INPUT(RIn));
  Comparator #(.width(4)) comparator_2 (.a(DR3), .b(SR2_2), .eq(comparator_2_eq));  // open: gt, lt
  Comparator #(.width(4)) comparator_3 (.a(DR3), .b(IR2[23:20]), .eq(comparator_3_eq));  // open: gt, lt
  // Probe on ALU3
  Multiplexer #(.width(32)) multiplexer_6 (.in0(ALU4), .in1(MEM4), .out(MEM5_FW), .sel(Control4[8]));  // open: en
  // Probe on MEM5_FW
  IF_IDRR_Buffer Buffer_1 (
    .PC_1(adder_1_out), .IR(ram_2_data), .Clock(and_3_out), .PC_1_2(PC2), .IR_2(IR2), .Buffer_Write(S));
  and and_3 (and_3_out, C, HALT);
  Comparator #(.width(32)) comparator_4 (.a(FA2), .b(FB2), .eq(comparator_4_eq));  // open: gt, lt
  and and_4 (and_4_out, 1'b1, comparator_4_eq);
  not not_3 (not_3_out, comparator_4_eq);
  and and_5 (and_5_out, not_3_out, 1'b1);
  // Probe on A2
  EX_MEM_Buffer ex_mem_buffer_1 (
    .CalcPC(CalcPC2), .ALU(ALU3), .Control(Control3), .DR(DR3), .B(B3), .Clock(C), .CalcPC_2(CalcPC4),
    .ALU_2(ALU4), .Control_2(Control4), .DR_2(DR4), .B_2(B4));
  MEM_WB_Buffer mem_wb_buffer_1 (
    .CalcPC(CalcPC4), .MEM(MEM4), .ALU(ALU4), .Control(Control4), .DR(DR4), .Clock(C), .CalcPC_2(CalcPC5),
    .MEM_2(MEM5), .ALU_2(ALU5), .Control_2(Control5), .DR_2(DR5));
  Multiplexer multiplexer_7 (.in0(and_4_out), .in1(and_5_out), .out(multiplexer_7_out), .sel(BNE));  // open: en
  IDRR_EX_Buffer idrr_ex_buffer_1 (
    .PC_1(PC2), .A(FA2), .B(FB2), .Control(multiplexer_5_out), .Offset(IR2[19:0]), .DR(IR2[27:24]),
    .SR1(IR2[23:20]), .SR2(SR2_2), .OP2(IR2[31:28]), .Buffer_Write(S), .Clock(C), .PC_1_2(PC3), .A_2(A3),
    .B_2(B3), .Control_2(Control3), .Offset_2(OFF3), .DR_2(DR3), .SR1_2(SR1_3), .SR2_2(SR2_3), .OP2_2(OP3));
  // Probe on B2
  Forwarding forwarding_1 (
    .ALU3(ALU3), .MEM4(MEM5_FW), .RIn(RIn), .SR1(IR2[23:20]), .DR3(DR3), .DR4(DR4), .DR5(DR5), .SR2(SR2_2),
    .A(A2), .B(B2), .F1(FA2), .F2(FB2));
  // Probe on FB2
  // Probe on {PCSel[1], JLR}
  Multiplexer multiplexer_8 (.in0(1'b0), .in1(multiplexer_7_out), .out(PCSel[1]), .sel(or_2_out));  // open: en
  Comparator #(.width(4)) comparator_5 (.a(IR2[31:28]), .b(4'b0011), .eq(comparator_5_eq));  // open: gt, lt
  Comparator #(.width(4)) comparator_6 (.a(IR2[31:28]), .b(4'b1001), .eq(comparator_6_eq));  // open: gt, lt
  or or_2 (or_2_out, comparator_5_eq, comparator_6_eq);

  // Other names for the same wires on the sheet: OFF_R = Control3[2]; func[1:0] = Control3[4:3]; MEMWr = Control4[7];
  //   MEM_ALU_4 = Control4[8]; RWr = Control5[1]; MEM_ALU_5 = Control5[8]; OFF2[19:0] = IR2[19:0];
  //   SR1_2[3:0] = IR2[23:20]; OP2[3:0] = IR2[31:28]; JALR[31:0] = FA2; PCSel[0] = JLR

  // Notes on the sheet:
  //   contents of rom_1 (hex, n*v repeats v):
  //   23 27 2a 5 63 126 26 a5 3e 25 5*0 220
endmodule

module Dual_Ported_Register_File (
  input  CLK,
  input  WrEN,
  input  [3:0] WrREGNO,
  input  [3:0] RdREGNO1,
  input  [3:0] RdREGNO2,
  input  [31:0] INPUT,
  output [31:0] OUT1,
  output [31:0] OUT2
);

  wire En_a0, En_a1, En_a2, En_at, En_fp, En_k0, En_ra, En_s0, En_s1, En_s2, En_sp, En_t0, En_t1, En_t2,
       En_v0;
  wire [31:0] a0, a1, a2, at, fp, k0, ra, s0, s1, s2, sp, t0, t1, t2, v0, zero;

  Decoder #(.select(4), .disabled(0)) decoder_1 (
    .out1(En_at), .out2(En_v0), .out3(En_a0), .out4(En_a1), .out5(En_a2), .out6(En_t0), .out7(En_t1),
    .out8(En_t2), .out9(En_s0), .out10(En_s1), .out11(En_s2), .out12(En_k0), .out13(En_sp), .out14(En_fp),
    .out15(En_ra), .sel(WrREGNO), .en(WrEN));  // open: out0
  Register #(.width(32)) u_zero (.D(INPUT), .en(1'b0), .Q(zero), .clk(CLK));  // open: clr
  Register #(.width(32)) u_at (.D(INPUT), .en(En_at), .Q(at), .clk(CLK));  // open: clr
  Register #(.width(32)) u_v0 (.D(INPUT), .en(En_v0), .Q(v0), .clk(CLK));  // open: clr
  Register #(.width(32)) u_a0 (.D(INPUT), .en(En_a0), .Q(a0), .clk(CLK));  // open: clr
  Register #(.width(32)) u_a1 (.D(INPUT), .en(En_a1), .Q(a1), .clk(CLK));  // open: clr
  Register #(.width(32)) u_a2 (.D(INPUT), .en(En_a2), .Q(a2), .clk(CLK));  // open: clr
  Register #(.width(32)) u_t0 (.D(INPUT), .en(En_t0), .Q(t0), .clk(CLK));  // open: clr
  Register #(.width(32)) u_t1 (.D(INPUT), .en(En_t1), .Q(t1), .clk(CLK));  // open: clr
  Multiplexer #(.select(4), .width(32), .disabled(0), .enable("false")) multiplexer_1 (
    .in0(zero), .in1(at), .in2(v0), .in3(a0), .in4(a1), .in5(a2), .in6(t0), .in7(t1), .in8(t2), .in9(s0),
    .in10(s1), .in11(s2), .in12(k0), .in13(sp), .in14(fp), .in15(ra), .out(OUT2), .sel(RdREGNO2));
  Register #(.width(32)) u_t2 (.D(INPUT), .en(En_t2), .Q(t2), .clk(CLK));  // open: clr
  Register #(.width(32)) u_s0 (.D(INPUT), .en(En_s0), .Q(s0), .clk(CLK));  // open: clr
  Register #(.width(32)) u_s1 (.D(INPUT), .en(En_s1), .Q(s1), .clk(CLK));  // open: clr
  Register #(.width(32)) u_s2 (.D(INPUT), .en(En_s2), .Q(s2), .clk(CLK));  // open: clr
  Register #(.width(32)) u_k0 (.D(INPUT), .en(En_k0), .Q(k0), .clk(CLK));  // open: clr
  Register #(.width(32)) u_sp (.D(INPUT), .en(En_sp), .Q(sp), .clk(CLK));  // open: clr
  Register #(.width(32)) u_fp (.D(INPUT), .en(En_fp), .Q(fp), .clk(CLK));  // open: clr
  Register #(.width(32)) u_ra (.D(INPUT), .en(En_ra), .Q(ra), .clk(CLK));  // open: clr
  Multiplexer #(.select(4), .width(32), .disabled(0), .enable("false")) multiplexer_2 (
    .in0(zero), .in1(at), .in2(v0), .in3(a0), .in4(a1), .in5(a2), .in6(t0), .in7(t1), .in8(t2), .in9(s0),
    .in10(s1), .in11(s2), .in12(k0), .in13(sp), .in14(fp), .in15(ra), .out(OUT1), .sel(RdREGNO1));

  // Notes on the sheet:
  //   MODIFY AT YOUR OWN RISK
endmodule

module IF_IDRR_Buffer (
  input  [31:0] PC_1,
  input  [31:0] IR,
  input  Clock,
  input  Buffer_Write,
  output [31:0] PC_1_2,
  output [31:0] IR_2
);

  Register #(.width(32)) u_IR (.D(IR), .en(Buffer_Write), .Q(IR_2), .clk(Clock));  // open: clr
  Register #(.width(32)) u_PC_1 (.D(PC_1), .en(Buffer_Write), .Q(PC_1_2), .clk(Clock));  // open: clr
endmodule

module IDRR_EX_Buffer (
  input  [31:0] PC_1,
  input  [31:0] A,
  input  [31:0] B,
  input  [9:0] Control,
  input  [19:0] Offset,
  input  [3:0] DR,
  input  [3:0] SR1,
  input  [3:0] SR2,
  input  [3:0] OP2,
  input  Clock,
  input  Buffer_Write,
  output [31:0] PC_1_2,
  output [31:0] A_2,
  output [31:0] B_2,
  output [9:0] Control_2,
  output [19:0] Offset_2,
  output [3:0] DR_2,
  output [3:0] SR1_2,
  output [3:0] SR2_2,
  output [3:0] OP2_2
);

  wire [3:0] multiplexer_1_out, multiplexer_2_out, multiplexer_3_out, multiplexer_4_out;

  Register #(.width(32)) u_PC_1 (.D(PC_1), .en(Buffer_Write), .Q(PC_1_2), .clk(Clock));  // open: clr
  Register #(.width(32)) register_1 (.D(A), .en(Buffer_Write), .Q(A_2), .clk(Clock));  // open: clr
  Register #(.width(32)) register_2 (.D(B), .en(Buffer_Write), .Q(B_2), .clk(Clock));  // open: clr
  Register #(.width(10)) register_3 (.D(Control), .en(Buffer_Write), .Q(Control_2), .clk(Clock));  // open: clr
  Register #(.width(20)) register_4 (.D(Offset), .en(Buffer_Write), .Q(Offset_2), .clk(Clock));  // open: clr
  Multiplexer #(.width(4)) multiplexer_1 (
    .in0(4'b0000), .in1(DR), .out(multiplexer_1_out), .sel(Buffer_Write));  // open: en
  Multiplexer #(.width(4)) multiplexer_2 (
    .in0(4'b0000), .in1(SR1), .out(multiplexer_2_out), .sel(Buffer_Write));  // open: en
  Multiplexer #(.width(4)) multiplexer_3 (
    .in0(4'b0000), .in1(SR2), .out(multiplexer_3_out), .sel(Buffer_Write));  // open: en
  Multiplexer #(.width(4)) multiplexer_4 (
    .in0(4'b0000), .in1(OP2), .out(multiplexer_4_out), .sel(Buffer_Write));  // open: en
  Register #(.width(4)) register_5 (.D(multiplexer_1_out), .Q(DR_2), .clk(Clock));  // open: en, clr
  Register #(.width(4)) register_6 (.D(multiplexer_2_out), .Q(SR1_2), .clk(Clock));  // open: en, clr
  Register #(.width(4)) register_7 (.D(multiplexer_3_out), .Q(SR2_2), .clk(Clock));  // open: en, clr
  Register #(.width(4)) register_8 (.D(multiplexer_4_out), .Q(OP2_2), .clk(Clock));  // open: en, clr
  // Probe on DR_2
  // Probe on OP2_2
endmodule

module EX_MEM_Buffer (
  input  [31:0] CalcPC,
  input  [31:0] ALU,
  input  [9:0] Control,
  input  [3:0] DR,
  input  [31:0] B,
  input  Clock,
  output [31:0] CalcPC_2,
  output [31:0] ALU_2,
  output [9:0] Control_2,
  output [3:0] DR_2,
  output [31:0] B_2
);

  wire undriven;

  Register #(.width(32)) PC_1 (.D(CalcPC), .en(undriven), .Q(CalcPC_2), .clk(Clock));  // open: clr
  Register #(.width(32)) register_1 (.D(ALU), .en(undriven), .Q(ALU_2), .clk(Clock));  // open: clr
  Register #(.width(10)) register_2 (.D(Control), .en(undriven), .Q(Control_2), .clk(Clock));  // open: clr
  Register #(.width(4)) register_3 (.D(DR), .en(undriven), .Q(DR_2), .clk(Clock));  // open: clr
  Register #(.width(32)) register_4 (.D(B), .Q(B_2), .clk(Clock));  // open: en, clr
endmodule

module MEM_WB_Buffer (
  input  [31:0] CalcPC,
  input  [31:0] MEM,
  input  [31:0] ALU,
  input  [9:0] Control,
  input  [3:0] DR,
  input  Clock,
  output [31:0] CalcPC_2,
  output [31:0] MEM_2,
  output [31:0] ALU_2,
  output [9:0] Control_2,
  output [3:0] DR_2
);

  wire undriven;

  Register #(.width(32)) PC_1 (.D(CalcPC), .en(undriven), .Q(CalcPC_2), .clk(Clock));  // open: clr
  Register #(.width(32)) register_1 (.D(MEM), .en(undriven), .Q(MEM_2), .clk(Clock));  // open: clr
  Register #(.width(32)) register_2 (.D(ALU), .en(undriven), .Q(ALU_2), .clk(Clock));  // open: clr
  Register #(.width(10)) register_3 (.D(Control), .en(undriven), .Q(Control_2), .clk(Clock));  // open: clr
  Register #(.width(4)) register_4 (.D(DR), .en(undriven), .Q(DR_2), .clk(Clock));  // open: clr
endmodule

module ALU (
  input  [1:0] func,
  input  [31:0] A,
  input  [31:0] B,
  output [31:0] out_4
);

  wire [31:0] A_1_10, ADD_00, NAND_01, SHIFT_11, shifter_1_out, shifter_2_out, shifter_3_out;

  Adder #(.width(32)) adder_1 (.a(A), .b(B), .out(ADD_00));  // open: cin, cout
  assign NAND_01 = ~(A & B);  // NAND_Gate nand_1, 32 bits wide
  Adder #(.width(32)) adder_2 (.a(A), .b(32'h1), .out(A_1_10));  // open: cin, cout
  Shifter #(.width(32)) shifter_1 (.in(A), .\dist (B[4:0]), .out(shifter_1_out));
  Shifter #(.width(32), .shift("lr")) shifter_2 (.in(A), .\dist (B[4:0]), .out(shifter_2_out));
  Shifter #(.width(32), .shift("ar")) shifter_3 (.in(A), .\dist (B[4:0]), .out(shifter_3_out));
  Multiplexer #(.select(2), .width(32), .disabled(0), .enable("false")) multiplexer_1 (
    .in0(ADD_00), .in1(NAND_01), .in2(A_1_10), .in3(SHIFT_11), .out(out_4), .sel(func));
  Multiplexer #(.select(2), .width(32), .disabled(0), .enable("false")) multiplexer_2 (
    .in0(shifter_1_out), .in1(shifter_1_out), .in2(shifter_2_out), .in3(shifter_3_out), .out(SHIFT_11),
    .sel(B[19:18]));
endmodule

module Forwarding (
  input  [31:0] A,
  input  [31:0] B,
  input  [31:0] ALU3,
  input  [31:0] MEM4,
  input  [31:0] RIn,
  input  [3:0] SR1,
  input  [3:0] DR3,
  input  [3:0] DR4,
  input  [3:0] DR5,
  input  [3:0] SR2,
  output [31:0] F1,
  output [31:0] F2
);

  wire comparator_1_eq, comparator_2_eq, comparator_3_eq, comparator_4_eq, comparator_5_eq, comparator_6_eq,
       not_1_out, not_2_out, or_2_out, or_4_out;
  wire [1:0] or_1_out, or_3_out;

  // Probe on SR1
  Comparator #(.width(4)) comparator_1 (.a(SR1), .b(DR3), .eq(comparator_1_eq));  // open: gt, lt
  or or_1 (or_1_out[0], comparator_1_eq, comparator_4_eq);
  not not_1 (not_1_out, comparator_1_eq);
  Comparator #(.width(4)) comparator_2 (.a(SR1), .b(DR4), .eq(comparator_2_eq));  // open: gt, lt
  Comparator #(.width(4)) comparator_3 (.a(SR2), .b(DR3), .eq(comparator_3_eq));  // open: gt, lt
  or or_2 (or_2_out, comparator_2_eq, comparator_4_eq);
  or or_3 (or_3_out[0], comparator_3_eq, comparator_6_eq);
  and and_1 (or_1_out[1], or_2_out, not_1_out);
  Comparator #(.width(4)) comparator_4 (.a(SR1), .b(DR5), .eq(comparator_4_eq));  // open: gt, lt
  or or_4 (or_4_out, comparator_5_eq, comparator_6_eq);
  not not_2 (not_2_out, comparator_3_eq);
  Comparator #(.width(4)) comparator_5 (.a(SR2), .b(DR4), .eq(comparator_5_eq));  // open: gt, lt
  and and_2 (or_3_out[1], or_4_out, not_2_out);
  Comparator #(.width(4)) comparator_6 (.a(SR2), .b(DR5), .eq(comparator_6_eq));  // open: gt, lt
  // Probe on or_3_out
  Multiplexer #(.select(2), .width(32)) multiplexer_1 (
    .in0(A), .in1(ALU3), .in2(MEM4), .in3(RIn), .out(F1), .sel(or_1_out));  // open: en
  // Probe on or_1_out
  Multiplexer #(.select(2), .width(32)) multiplexer_2 (
    .in0(B), .in1(ALU3), .in2(MEM4), .in3(RIn), .out(F2), .sel(or_3_out));  // open: en
endmodule
